# Fritzing sketch Dillo_Sawppy_Motor_Drivers (saved by Fritzing 0.9.3b)

parts:
  J1 = Power Jack [package=power_jack_slot]
  M1 = DC Motor
  M3 = DC Motor
  M5 = DC Motor
  M6 = DC Motor
  Part1 = Arduino Mega ADK (Rev3)
  S2 = H-Bridge with L298N
  S3 = H-Bridge with L298N
  M7 = DC Motor
  S1 = H-Bridge with L298N
  M2 = DC Motor

nets:
  GND: J1.GND, S2.GND, S3.GND
  12V: J1.PWR, S2.12V, S3.12V
  N1: M1.pin_1, S2.OUT3-Motor2
  N2: M1.pin_2, S2.OUT4-Motor2
  N3: M3.pin_1, S1.OUT3-Motor2
  N4: M5.pin_1, S3.OUT3-Motor2
  N5: M5.pin_2, S3.OUT4-Motor2
  N6: M6.pin_1, S3.OUT1-Motor1
  N7: M6.pin_2, S3.OUT2-Motor1
  N8: Part1.D13_PWM, S1.IN1
  N9: Part1.D12_PWM, S1.IN2
  N10: Part1.D11_PWM, S1.IN3
  N11: Part1.D10_PWM, S1.IN4
  N12: Part1.D9_PWM, S2.IN1
  N13: Part1.D8_PWM, S2.IN2
  N14: Part1.D2_PWM, S3.IN4
  N15: Part1.D3_PWM, S3.IN3
  N16: Part1.D4_PWM, S3.IN2
  N17: Part1.D5_PWM, S3.IN1
  N18: Part1.D6_PWM, S2.IN4
  N19: Part1.D7_PWM, S2.IN3
  N20: S2.OUT1-Motor1, M7.pin_1
  N21: S2.OUT2-Motor1, M7.pin_2
  N22: S1.OUT1-Motor1, M2.pin_1
  N23: S1.OUT2-Motor1, M2.pin_2

custom parts:
  H-Bridge with L298N: h-bridge
